// Logisim project 262proj.circ as structural Verilog
module main (
);

  wire milli_1_millireset, Reset_out, second_1_secondreset, sign_1_sign, Split_out, Start_Stop_out;
  wire [3:0] MST, MSU, MT, MU, splitting_records_1_s1_carry_out_1, splitting_records_1_s1_carry_out_2,
       splitting_records_1_s1_carry_out_3, splitting_records_1_s1_carry_out_4,
       splitting_records_1_s1_carry_out_5, splitting_records_1_s1_carry_out_6,
       splitting_records_1_s2_carry_out_1, splitting_records_1_s2_carry_out_2,
       splitting_records_1_s2_carry_out_3, splitting_records_1_s2_carry_out_4,
       splitting_records_1_s2_carry_out_5, splitting_records_1_s2_carry_out_6,
       splitting_records_1_s3_carry_out_1, splitting_records_1_s3_carry_out_2,
       splitting_records_1_s3_carry_out_3, splitting_records_1_s3_carry_out_4,
       splitting_records_1_s3_carry_out_5, splitting_records_1_s3_carry_out_6,
       splitting_records_1_s4_carry_out_1, splitting_records_1_s4_carry_out_2,
       splitting_records_1_s4_carry_out_3, splitting_records_1_s4_carry_out_4,
       splitting_records_1_s4_carry_out_5, splitting_records_1_s4_carry_out_6,
       splitting_records_1_s5_carry_out_1, splitting_records_1_s5_carry_out_2,
       splitting_records_1_s5_carry_out_3, splitting_records_1_s5_carry_out_4,
       splitting_records_1_s5_carry_out_5, splitting_records_1_s5_carry_out_6,
       splitting_records_1_s6_carry_out_1, splitting_records_1_s6_carry_out_2,
       splitting_records_1_s6_carry_out_3, splitting_records_1_s6_carry_out_4,
       splitting_records_1_s6_carry_out_5, splitting_records_1_s6_carry_out_6, ST, SU;

  Button Start_Stop (.out(Start_Stop_out));
  Sign sign_1 (.SS(Start_Stop_out), .Sign(sign_1_sign));
  Milli milli_1 (
    .Sign(sign_1_sign), .Reset(Reset_out), .MilliUnits(MSU), .MilliReset(milli_1_millireset), .MilliTens(MST));
  Second second_1 (
    .MilliReset(milli_1_millireset), .Reset(Reset_out), .SecondUnits(SU), .SecondReset(second_1_secondreset),
    .SecondTens(ST));
  Minute minute_1 (.SecondReset(second_1_secondreset), .Reset(Reset_out), .MinuteUnits(MU), .MinuteTens(MT));
  Button Split (.out(Split_out));
  Button Reset (.out(Reset_out));
  LED led_1 (.in(sign_1_sign));
  Splitting_Records splitting_records_1 (
    .Split(Split_out), .Reset(Reset_out), .Carry_in_1(MSU), .Carry_in_2(MST), .Carry_in_3(SU),
    .Carry_in_4(ST), .Carry_in_5(MU), .Carry_in_6(MT), .S6_Carry_out_1(splitting_records_1_s6_carry_out_1),
    .S6_Carry_out_2(splitting_records_1_s6_carry_out_2), .S6_Carry_out_3(splitting_records_1_s6_carry_out_3),
    .S6_Carry_out_4(splitting_records_1_s6_carry_out_4), .S6_Carry_out_5(splitting_records_1_s6_carry_out_5),
    .S6_Carry_out_6(splitting_records_1_s6_carry_out_6), .S5_Carry_out_1(splitting_records_1_s5_carry_out_1),
    .S5_Carry_out_2(splitting_records_1_s5_carry_out_2), .S5_Carry_out_3(splitting_records_1_s5_carry_out_3),
    .S5_Carry_out_4(splitting_records_1_s5_carry_out_4), .S5_Carry_out_5(splitting_records_1_s5_carry_out_5),
    .S5_Carry_out_6(splitting_records_1_s5_carry_out_6), .S4_Carry_out_1(splitting_records_1_s4_carry_out_1),
    .S4_Carry_out_2(splitting_records_1_s4_carry_out_2), .S4_Carry_out_3(splitting_records_1_s4_carry_out_3),
    .S4_Carry_out_4(splitting_records_1_s4_carry_out_4), .S4_Carry_out_5(splitting_records_1_s4_carry_out_5),
    .S4_Carry_out_6(splitting_records_1_s4_carry_out_6), .S3_Carry_out_1(splitting_records_1_s3_carry_out_1),
    .S3_Carry_out_2(splitting_records_1_s3_carry_out_2), .S3_Carry_out_3(splitting_records_1_s3_carry_out_3),
    .S3_Carry_out_4(splitting_records_1_s3_carry_out_4), .S3_Carry_out_5(splitting_records_1_s3_carry_out_5),
    .S3_Carry_out_6(splitting_records_1_s3_carry_out_6), .S2_Carry_out_1(splitting_records_1_s2_carry_out_1),
    .S2_Carry_out_2(splitting_records_1_s2_carry_out_2), .S2_Carry_out_3(splitting_records_1_s2_carry_out_3),
    .S2_Carry_out_4(splitting_records_1_s2_carry_out_4), .S2_Carry_out_5(splitting_records_1_s2_carry_out_5),
    .S2_Carry_out_6(splitting_records_1_s2_carry_out_6), .S1_Carry_out_1(splitting_records_1_s1_carry_out_1),
    .S1_Carry_out_2(splitting_records_1_s1_carry_out_2), .S1_Carry_out_3(splitting_records_1_s1_carry_out_3),
    .S1_Carry_out_4(splitting_records_1_s1_carry_out_4), .S1_Carry_out_5(splitting_records_1_s1_carry_out_5),
    .S1_Carry_out_6(splitting_records_1_s1_carry_out_6));
  Hex_Digit_Display hex_digit_display_1 (.value(MT));  // open: dp
  Hex_Digit_Display hex_digit_display_2 (.value(MU));  // open: dp
  Hex_Digit_Display hex_digit_display_3 (.value(splitting_records_1_s6_carry_out_6));  // open: dp
  Hex_Digit_Display hex_digit_display_4 (.value(splitting_records_1_s6_carry_out_5));  // open: dp
  Hex_Digit_Display hex_digit_display_5 (.value(splitting_records_1_s5_carry_out_6));  // open: dp
  Hex_Digit_Display hex_digit_display_6 (.value(splitting_records_1_s5_carry_out_5));  // open: dp
  Hex_Digit_Display hex_digit_display_7 (.value(splitting_records_1_s4_carry_out_6));  // open: dp
  Hex_Digit_Display hex_digit_display_8 (.value(splitting_records_1_s4_carry_out_5));  // open: dp
  Hex_Digit_Display hex_digit_display_9 (.value(splitting_records_1_s3_carry_out_6));  // open: dp
  Hex_Digit_Display hex_digit_display_10 (.value(splitting_records_1_s3_carry_out_5));  // open: dp
  Hex_Digit_Display hex_digit_display_11 (.value(splitting_records_1_s2_carry_out_6));  // open: dp
  Hex_Digit_Display hex_digit_display_12 (.value(splitting_records_1_s2_carry_out_5));  // open: dp
  Hex_Digit_Display hex_digit_display_13 (.value(splitting_records_1_s1_carry_out_6));  // open: dp
  Hex_Digit_Display hex_digit_display_14 (.value(splitting_records_1_s1_carry_out_5));  // open: dp
  Hex_Digit_Display hex_digit_display_15 (.value(ST));  // open: dp
  Hex_Digit_Display hex_digit_display_16 (.value(splitting_records_1_s6_carry_out_4));  // open: dp
  Hex_Digit_Display hex_digit_display_17 (.value(splitting_records_1_s5_carry_out_4));  // open: dp
  Hex_Digit_Display hex_digit_display_18 (.value(splitting_records_1_s4_carry_out_4));  // open: dp
  Hex_Digit_Display hex_digit_display_19 (.value(splitting_records_1_s3_carry_out_4));  // open: dp
  Hex_Digit_Display hex_digit_display_20 (.value(splitting_records_1_s2_carry_out_4));  // open: dp
  Hex_Digit_Display hex_digit_display_21 (.value(splitting_records_1_s1_carry_out_4));  // open: dp
  Hex_Digit_Display hex_digit_display_22 (.value(MST));  // open: dp
  Hex_Digit_Display hex_digit_display_23 (.value(SU));  // open: dp
  Hex_Digit_Display hex_digit_display_24 (.value(splitting_records_1_s6_carry_out_2));  // open: dp
  Hex_Digit_Display hex_digit_display_25 (.value(splitting_records_1_s6_carry_out_3));  // open: dp
  Hex_Digit_Display hex_digit_display_26 (.value(splitting_records_1_s5_carry_out_2));  // open: dp
  Hex_Digit_Display hex_digit_display_27 (.value(splitting_records_1_s5_carry_out_3));  // open: dp
  Hex_Digit_Display hex_digit_display_28 (.value(splitting_records_1_s4_carry_out_2));  // open: dp
  Hex_Digit_Display hex_digit_display_29 (.value(splitting_records_1_s4_carry_out_3));  // open: dp
  Hex_Digit_Display hex_digit_display_30 (.value(splitting_records_1_s3_carry_out_2));  // open: dp
  Hex_Digit_Display hex_digit_display_31 (.value(splitting_records_1_s3_carry_out_3));  // open: dp
  Hex_Digit_Display hex_digit_display_32 (.value(splitting_records_1_s2_carry_out_2));  // open: dp
  Hex_Digit_Display hex_digit_display_33 (.value(splitting_records_1_s2_carry_out_3));  // open: dp
  Hex_Digit_Display hex_digit_display_34 (.value(splitting_records_1_s1_carry_out_2));  // open: dp
  Hex_Digit_Display hex_digit_display_35 (.value(splitting_records_1_s1_carry_out_3));  // open: dp
  Hex_Digit_Display hex_digit_display_36 (.value(MSU));  // open: dp
  Hex_Digit_Display hex_digit_display_37 (.value(splitting_records_1_s6_carry_out_1));  // open: dp
  Hex_Digit_Display hex_digit_display_38 (.value(splitting_records_1_s5_carry_out_1));  // open: dp
  Hex_Digit_Display hex_digit_display_39 (.value(splitting_records_1_s4_carry_out_1));  // open: dp
  Hex_Digit_Display hex_digit_display_40 (.value(splitting_records_1_s3_carry_out_1));  // open: dp
  Hex_Digit_Display hex_digit_display_41 (.value(splitting_records_1_s2_carry_out_1));  // open: dp
  Hex_Digit_Display hex_digit_display_42 (.value(splitting_records_1_s1_carry_out_1));  // open: dp

  // Notes on the sheet:
  //   .
  //   Elapsed Time
  //   .
  //   .
  //   Split Time
  //   Split 6
  //   .
  //   .
  //   Split 5
  //   .
  //   .
  //   Split 4
  //   .
  //   .
  //   Split 3
  //   .
  //   .
  //   Split 2
  //   .
  //   .
  //   Split 1
  //   .
  //   .
  //   .
  //   .
  //   .
  //   .
  //   .
  //   .
  //   .
  //   .
  //   .
  //   .
  //   .
  //   .
  //   .
endmodule

module Second (
  input  MilliReset,
  input  Reset,
  output [3:0] SecondUnits,
  output SecondReset,
  output [3:0] SecondTens
);

  wire and_1_out, and_2_out, and_3_out, and_4_out, and_5_out, and_6_out, and_7_out, and_8_out, and_9_out,
       j_k_ff_6_qn, j_k_ff_7_qn, not_1_out, or_1_out, or_2_out;

  J_K_Flip_Flop j_k_ff_1 (
    .J(MilliReset), .K(MilliReset), .clk(MilliReset), .Q(SecondUnits[0]), .reset(Reset));  // open: Qn, preset
  and and_1 (and_1_out, SecondUnits[0], SecondUnits[3]);
  not not_1 (not_1_out, and_1_out);
  and and_2 (and_2_out, SecondUnits[0], j_k_ff_6_qn);
  J_K_Flip_Flop j_k_ff_2 (
    .J(not_1_out), .K(not_1_out), .clk(not_1_out), .Q(SecondTens[0]), .reset(Reset));  // open: Qn, preset
  J_K_Flip_Flop j_k_ff_3 (
    .J(and_2_out), .K(and_2_out), .clk(MilliReset), .Q(SecondUnits[1]), .reset(Reset));  // open: Qn, preset
  and and_3 (and_3_out, SecondTens[0], j_k_ff_7_qn);
  and and_4 (and_4_out, SecondUnits[0], SecondUnits[1]);
  J_K_Flip_Flop j_k_ff_4 (
    .J(and_4_out), .K(and_4_out), .clk(MilliReset), .Q(SecondUnits[2]), .reset(Reset));  // open: Qn, preset
  J_K_Flip_Flop j_k_ff_5 (
    .J(and_3_out), .K(and_3_out), .clk(not_1_out), .Q(SecondTens[1]), .reset(Reset));  // open: Qn, preset
  and and_5 (and_5_out, SecondTens[2], SecondTens[0]);
  and and_6 (and_6_out, SecondTens[0], SecondTens[1]);
  and and_7 (and_7_out, SecondUnits[3], SecondUnits[0]);
  and and_8 (and_8_out, and_4_out, SecondUnits[2]);
  or or_1 (or_1_out, and_5_out, and_6_out);
  or or_2 (or_2_out, and_7_out, and_8_out);
  J_K_Flip_Flop j_k_ff_6 (
    .J(or_2_out), .K(or_2_out), .clk(MilliReset), .Q(SecondUnits[3]), .Qn(j_k_ff_6_qn), .reset(Reset));  // open: preset
  J_K_Flip_Flop j_k_ff_7 (
    .J(or_1_out), .K(or_1_out), .clk(not_1_out), .Q(SecondTens[2]), .Qn(j_k_ff_7_qn), .reset(Reset));  // open: preset
  and and_9 (and_9_out, SecondTens[0], SecondTens[2]);
  not not_2 (SecondReset, and_9_out);

  assign SecondTens[3] = 1'b0;
endmodule

module Minute (
  input  SecondReset,
  input  Reset,
  output [3:0] MinuteUnits,
  output [3:0] MinuteTens
);

  wire and_1_out, and_2_out, and_3_out, and_4_out, and_5_out, and_6_out, and_7_out, and_8_out, and_9_out,
       j_k_ff_7_qn, j_k_ff_8_qn, not_1_out, or_1_out, or_2_out;

  J_K_Flip_Flop j_k_ff_1 (
    .J(SecondReset), .K(SecondReset), .clk(SecondReset), .Q(MinuteUnits[0]), .reset(Reset));  // open: Qn, preset
  and and_1 (and_1_out, MinuteUnits[0], MinuteUnits[3]);
  not not_1 (not_1_out, and_1_out);
  and and_2 (and_2_out, MinuteUnits[0], j_k_ff_7_qn);
  J_K_Flip_Flop j_k_ff_2 (
    .J(not_1_out), .K(not_1_out), .clk(not_1_out), .Q(MinuteTens[0]), .reset(Reset));  // open: Qn, preset
  J_K_Flip_Flop j_k_ff_3 (
    .J(and_2_out), .K(and_2_out), .clk(SecondReset), .Q(MinuteUnits[1]), .reset(Reset));  // open: Qn, preset
  and and_3 (and_3_out, MinuteTens[0], j_k_ff_8_qn);
  and and_4 (and_4_out, MinuteUnits[0], MinuteUnits[1]);
  J_K_Flip_Flop j_k_ff_4 (
    .J(and_4_out), .K(and_4_out), .clk(SecondReset), .Q(MinuteUnits[2]), .reset(Reset));  // open: Qn, preset
  J_K_Flip_Flop j_k_ff_5 (
    .J(and_3_out), .K(and_3_out), .clk(not_1_out), .Q(MinuteTens[1]), .reset(Reset));  // open: Qn, preset
  and and_5 (and_5_out, MinuteUnits[3], MinuteUnits[0]);
  and and_6 (and_6_out, and_4_out, MinuteUnits[2]);
  and and_7 (and_7_out, MinuteTens[0], MinuteTens[1]);
  J_K_Flip_Flop j_k_ff_6 (
    .J(and_7_out), .K(and_7_out), .clk(not_1_out), .Q(MinuteTens[2]), .reset(Reset));  // open: Qn, preset
  or or_1 (or_1_out, and_5_out, and_6_out);
  J_K_Flip_Flop j_k_ff_7 (
    .J(or_1_out), .K(or_1_out), .clk(SecondReset), .Q(MinuteUnits[3]), .Qn(j_k_ff_7_qn), .reset(Reset));  // open: preset
  and and_8 (and_8_out, MinuteTens[3], MinuteTens[0]);
  and and_9 (and_9_out, and_7_out, MinuteTens[2]);
  or or_2 (or_2_out, and_8_out, and_9_out);
  J_K_Flip_Flop j_k_ff_8 (
    .J(or_2_out), .K(or_2_out), .clk(not_1_out), .Q(MinuteTens[3]), .Qn(j_k_ff_8_qn), .reset(Reset));  // open: preset
endmodule

module Milli (
  input  Sign,
  input  Reset,
  output [3:0] MilliUnits,
  output MilliReset,
  output [3:0] MilliTens
);

  wire and_1_out, and_2_out, and_3_out, and_4_out, and_5_out, and_6_out, and_7_out, and_8_out, and_9_out,
       and_10_out, and_11_out, clock_1_out, j_k_ff_7_qn, j_k_ff_8_qn, not_1_out, or_1_out, or_2_out;

  Clock clock_1 (.out(clock_1_out));
  J_K_Flip_Flop j_k_ff_1 (.J(Sign), .K(Sign), .clk(and_1_out), .Q(MilliUnits[0]), .reset(Reset));  // open: Qn, preset
  and and_1 (and_1_out, Sign, clock_1_out);
  and and_2 (and_2_out, MilliUnits[0], MilliUnits[3]);
  not not_1 (not_1_out, and_2_out);
  and and_3 (and_3_out, MilliUnits[0], j_k_ff_7_qn);
  J_K_Flip_Flop j_k_ff_2 (
    .J(not_1_out), .K(not_1_out), .clk(not_1_out), .Q(MilliTens[0]), .reset(Reset));  // open: Qn, preset
  J_K_Flip_Flop j_k_ff_3 (
    .J(and_3_out), .K(and_3_out), .clk(and_1_out), .Q(MilliUnits[1]), .reset(Reset));  // open: Qn, preset
  and and_4 (and_4_out, MilliTens[0], j_k_ff_8_qn);
  and and_5 (and_5_out, MilliUnits[0], MilliUnits[1]);
  J_K_Flip_Flop j_k_ff_4 (
    .J(and_5_out), .K(and_5_out), .clk(and_1_out), .Q(MilliUnits[2]), .reset(Reset));  // open: Qn, preset
  J_K_Flip_Flop j_k_ff_5 (
    .J(and_4_out), .K(and_4_out), .clk(not_1_out), .Q(MilliTens[1]), .reset(Reset));  // open: Qn, preset
  and and_6 (and_6_out, MilliUnits[3], MilliUnits[0]);
  and and_7 (and_7_out, and_5_out, MilliUnits[2]);
  and and_8 (and_8_out, MilliTens[0], MilliTens[1]);
  J_K_Flip_Flop j_k_ff_6 (
    .J(and_8_out), .K(and_8_out), .clk(not_1_out), .Q(MilliTens[2]), .reset(Reset));  // open: Qn, preset
  or or_1 (or_1_out, and_6_out, and_7_out);
  J_K_Flip_Flop j_k_ff_7 (
    .J(or_1_out), .K(or_1_out), .clk(and_1_out), .Q(MilliUnits[3]), .Qn(j_k_ff_7_qn), .reset(Reset));  // open: preset
  and and_9 (and_9_out, MilliTens[3], MilliTens[0]);
  and and_10 (and_10_out, and_8_out, MilliTens[2]);
  or or_2 (or_2_out, and_9_out, and_10_out);
  J_K_Flip_Flop j_k_ff_8 (
    .J(or_2_out), .K(or_2_out), .clk(not_1_out), .Q(MilliTens[3]), .Qn(j_k_ff_8_qn), .reset(Reset));  // open: preset
  and and_11 (and_11_out, MilliTens[0], MilliTens[3]);
  not not_2 (MilliReset, and_11_out);
endmodule

module Splitting (
  input  Split,
  input  Reset,
  input  [3:0] Carry_in_1,
  input  [3:0] Carry_in_2,
  input  [3:0] Carry_in_3,
  input  [3:0] Carry_in_4,
  input  [3:0] Carry_in_5,
  input  [3:0] Carry_in_6,
  output [3:0] Carry_out_1,
  output [3:0] Carry_out_2,
  output [3:0] Carry_out_3,
  output [3:0] Carry_out_4,
  output [3:0] Carry_out_5,
  output [3:0] Carry_out_6
);

  D_Flip_Flop d_ff_1 (.D(Carry_in_1[0]), .clk(Split), .Q(Carry_out_1[0]), .reset(Reset));  // open: Qn, preset
  D_Flip_Flop d_ff_2 (.D(Carry_in_1[1]), .clk(Split), .Q(Carry_out_1[1]), .reset(Reset));  // open: Qn, preset
  D_Flip_Flop d_ff_3 (.D(Carry_in_1[2]), .clk(Split), .Q(Carry_out_1[2]), .reset(Reset));  // open: Qn, preset
  D_Flip_Flop d_ff_4 (.D(Carry_in_1[3]), .clk(Split), .Q(Carry_out_1[3]), .reset(Reset));  // open: Qn, preset
  D_Flip_Flop d_ff_5 (.D(Carry_in_2[0]), .clk(Split), .Q(Carry_out_2[0]), .reset(Reset));  // open: Qn, preset
  D_Flip_Flop d_ff_6 (.D(Carry_in_2[1]), .clk(Split), .Q(Carry_out_2[1]), .reset(Reset));  // open: Qn, preset
  D_Flip_Flop d_ff_7 (.D(Carry_in_2[2]), .clk(Split), .Q(Carry_out_2[2]), .reset(Reset));  // open: Qn, preset
  D_Flip_Flop d_ff_8 (.D(Carry_in_2[3]), .clk(Split), .Q(Carry_out_2[3]), .reset(Reset));  // open: Qn, preset
  D_Flip_Flop d_ff_9 (.D(Carry_in_3[0]), .clk(Split), .Q(Carry_out_3[0]), .reset(Reset));  // open: Qn, preset
  D_Flip_Flop d_ff_10 (.D(Carry_in_3[1]), .clk(Split), .Q(Carry_out_3[1]), .reset(Reset));  // open: Qn, preset
  D_Flip_Flop d_ff_11 (.D(Carry_in_3[2]), .clk(Split), .Q(Carry_out_3[2]), .reset(Reset));  // open: Qn, preset
  D_Flip_Flop d_ff_12 (.D(Carry_in_3[3]), .clk(Split), .Q(Carry_out_3[3]), .reset(Reset));  // open: Qn, preset
  D_Flip_Flop d_ff_13 (.D(Carry_in_4[0]), .clk(Split), .Q(Carry_out_4[0]), .reset(Reset));  // open: Qn, preset
  D_Flip_Flop d_ff_14 (.D(Carry_in_4[1]), .clk(Split), .Q(Carry_out_4[1]), .reset(Reset));  // open: Qn, preset
  D_Flip_Flop d_ff_15 (.D(Carry_in_4[2]), .clk(Split), .Q(Carry_out_4[2]), .reset(Reset));  // open: Qn, preset
  D_Flip_Flop d_ff_16 (.D(Carry_in_4[3]), .clk(Split), .Q(Carry_out_4[3]), .reset(Reset));  // open: Qn, preset
  D_Flip_Flop d_ff_17 (.D(Carry_in_5[0]), .clk(Split), .Q(Carry_out_5[0]), .reset(Reset));  // open: Qn, preset
  D_Flip_Flop d_ff_18 (.D(Carry_in_5[1]), .clk(Split), .Q(Carry_out_5[1]), .reset(Reset));  // open: Qn, preset
  D_Flip_Flop d_ff_19 (.D(Carry_in_5[2]), .clk(Split), .Q(Carry_out_5[2]), .reset(Reset));  // open: Qn, preset
  D_Flip_Flop d_ff_20 (.D(Carry_in_5[3]), .clk(Split), .Q(Carry_out_5[3]), .reset(Reset));  // open: Qn, preset
  D_Flip_Flop d_ff_21 (.D(Carry_in_6[0]), .clk(Split), .Q(Carry_out_6[0]), .reset(Reset));  // open: Qn, preset
  D_Flip_Flop d_ff_22 (.D(Carry_in_6[1]), .clk(Split), .Q(Carry_out_6[1]), .reset(Reset));  // open: Qn, preset
  D_Flip_Flop d_ff_23 (.D(Carry_in_6[2]), .clk(Split), .Q(Carry_out_6[2]), .reset(Reset));  // open: Qn, preset
  D_Flip_Flop d_ff_24 (.D(Carry_in_6[3]), .clk(Split), .Q(Carry_out_6[3]), .reset(Reset));  // open: Qn, preset

  // Notes on the sheet:
  //   Ms
  //   Sec
  //   Min
endmodule

module Sign (
  input  SS,
  output Sign
);

  T_Flip_Flop t_ff_1 (.T(SS), .clk(SS), .Q(Sign));  // open: Qn, reset, preset

  // Notes on the sheet:
  //   Start/Stop
endmodule

module Splitting_Records (
  input  Split,
  input  Reset,
  input  [3:0] Carry_in_1,
  input  [3:0] Carry_in_2,
  input  [3:0] Carry_in_3,
  input  [3:0] Carry_in_4,
  input  [3:0] Carry_in_5,
  input  [3:0] Carry_in_6,
  output [3:0] S6_Carry_out_1,
  output [3:0] S6_Carry_out_2,
  output [3:0] S6_Carry_out_3,
  output [3:0] S6_Carry_out_4,
  output [3:0] S6_Carry_out_5,
  output [3:0] S6_Carry_out_6,
  output [3:0] S5_Carry_out_1,
  output [3:0] S5_Carry_out_2,
  output [3:0] S5_Carry_out_3,
  output [3:0] S5_Carry_out_4,
  output [3:0] S5_Carry_out_5,
  output [3:0] S5_Carry_out_6,
  output [3:0] S4_Carry_out_1,
  output [3:0] S4_Carry_out_2,
  output [3:0] S4_Carry_out_3,
  output [3:0] S4_Carry_out_4,
  output [3:0] S4_Carry_out_5,
  output [3:0] S4_Carry_out_6,
  output [3:0] S3_Carry_out_1,
  output [3:0] S3_Carry_out_2,
  output [3:0] S3_Carry_out_3,
  output [3:0] S3_Carry_out_4,
  output [3:0] S3_Carry_out_5,
  output [3:0] S3_Carry_out_6,
  output [3:0] S2_Carry_out_1,
  output [3:0] S2_Carry_out_2,
  output [3:0] S2_Carry_out_3,
  output [3:0] S2_Carry_out_4,
  output [3:0] S2_Carry_out_5,
  output [3:0] S2_Carry_out_6,
  output [3:0] S1_Carry_out_1,
  output [3:0] S1_Carry_out_2,
  output [3:0] S1_Carry_out_3,
  output [3:0] S1_Carry_out_4,
  output [3:0] S1_Carry_out_5,
  output [3:0] S1_Carry_out_6
);

  Splitting splitting_1 (
    .Split(Split), .Reset(Reset), .Carry_in_1(Carry_in_1), .Carry_in_2(Carry_in_2), .Carry_in_3(Carry_in_3),
    .Carry_in_4(Carry_in_4), .Carry_in_5(Carry_in_5), .Carry_in_6(Carry_in_6), .Carry_out_1(S1_Carry_out_1),
    .Carry_out_2(S1_Carry_out_2), .Carry_out_3(S1_Carry_out_3), .Carry_out_4(S1_Carry_out_4),
    .Carry_out_5(S1_Carry_out_5), .Carry_out_6(S1_Carry_out_6));
  Splitting splitting_2 (
    .Split(Split), .Reset(Reset), .Carry_in_1(S1_Carry_out_1), .Carry_in_2(S1_Carry_out_2),
    .Carry_in_3(S1_Carry_out_3), .Carry_in_4(S1_Carry_out_4), .Carry_in_5(S1_Carry_out_5),
    .Carry_in_6(S1_Carry_out_6), .Carry_out_1(S2_Carry_out_1), .Carry_out_2(S2_Carry_out_2),
    .Carry_out_3(S2_Carry_out_3), .Carry_out_4(S2_Carry_out_4), .Carry_out_5(S2_Carry_out_5),
    .Carry_out_6(S2_Carry_out_6));
  Splitting splitting_3 (
    .Split(Split), .Reset(Reset), .Carry_in_1(S2_Carry_out_1), .Carry_in_2(S2_Carry_out_2),
    .Carry_in_3(S2_Carry_out_3), .Carry_in_4(S2_Carry_out_4), .Carry_in_5(S2_Carry_out_5),
    .Carry_in_6(S2_Carry_out_6), .Carry_out_1(S3_Carry_out_1), .Carry_out_2(S3_Carry_out_2),
    .Carry_out_3(S3_Carry_out_3), .Carry_out_4(S3_Carry_out_4), .Carry_out_5(S3_Carry_out_5),
    .Carry_out_6(S3_Carry_out_6));
  Splitting splitting_4 (
    .Split(Split), .Reset(Reset), .Carry_in_1(S3_Carry_out_1), .Carry_in_2(S3_Carry_out_2),
    .Carry_in_3(S3_Carry_out_3), .Carry_in_4(S3_Carry_out_4), .Carry_in_5(S3_Carry_out_5),
    .Carry_in_6(S3_Carry_out_6), .Carry_out_1(S4_Carry_out_1), .Carry_out_2(S4_Carry_out_2),
    .Carry_out_3(S4_Carry_out_3), .Carry_out_4(S4_Carry_out_4), .Carry_out_5(S4_Carry_out_5),
    .Carry_out_6(S4_Carry_out_6));
  Splitting splitting_5 (
    .Split(Split), .Reset(Reset), .Carry_in_1(S4_Carry_out_1), .Carry_in_2(S4_Carry_out_2),
    .Carry_in_3(S4_Carry_out_3), .Carry_in_4(S4_Carry_out_4), .Carry_in_5(S4_Carry_out_5),
    .Carry_in_6(S4_Carry_out_6), .Carry_out_1(S5_Carry_out_1), .Carry_out_2(S5_Carry_out_2),
    .Carry_out_3(S5_Carry_out_3), .Carry_out_4(S5_Carry_out_4), .Carry_out_5(S5_Carry_out_5),
    .Carry_out_6(S5_Carry_out_6));
  Splitting splitting_6 (
    .Split(Split), .Reset(Reset), .Carry_in_1(S5_Carry_out_1), .Carry_in_2(S5_Carry_out_2),
    .Carry_in_3(S5_Carry_out_3), .Carry_in_4(S5_Carry_out_4), .Carry_in_5(S5_Carry_out_5),
    .Carry_in_6(S5_Carry_out_6), .Carry_out_1(S6_Carry_out_1), .Carry_out_2(S6_Carry_out_2),
    .Carry_out_3(S6_Carry_out_3), .Carry_out_4(S6_Carry_out_4), .Carry_out_5(S6_Carry_out_5),
    .Carry_out_6(S6_Carry_out_6));
endmodule
